# Fritzing sketch ContadorDisplay_0-9 (saved by Fritzing 0.9.3b)
breadboards: 1

parts:
  DI1 = 7-Segment LED Display [package=THT]
  Componente1 = Arduino Uno (Rev3) - ICSP
  R1 = Resistor [tolerance=±5% resistance=220 package=THT]
  R2 = Resistor [tolerance=±5% resistance=220 package=THT]
  R3 = Resistor [tolerance=±5% resistance=220 package=THT]
  R4 = Resistor [tolerance=±5% resistance=220 package=THT]
  R5 = Resistor [tolerance=±5% resistance=220 package=THT]
  R6 = Resistor [tolerance=±5% resistance=220 package=THT]
  part = Resistor [tolerance=±5% resistance=220 package=THT]

nets (from the schematic view):
  N1: DI1.cathodeE, R2.Pin_1
  N2: DI1.cathodeD, R1.Pin_1
  N3: DI1.commAnode#2, Componente1.GND
  N4: DI1.cathodeC, R3.Pin_0
  N5: DI1.cathodeB, part.Pin_0
  N6: DI1.cathodeA, R6.Pin_0
  N7: DI1.cathodeF, R4.Pin_1
  N8: DI1.cathodeG, R5.Pin_1
  N9: Componente1.D8, R5.Pin_0
  N10: Componente1.D2, part.Pin_1
  N11: Componente1.D3_PWM, R6.Pin_1
  N12: Componente1.D4, R3.Pin_1
  N13: Componente1.D5_PWM, R1.Pin_0
  N14: Componente1.D6_PWM, R2.Pin_0
  N15: Componente1.D7, R4.Pin_0
